# Fritzing sketch Arduino Data Logger 0.3 (saved by Fritzing 0.9.3b)
breadboards: 1

parts:
  Arduino = Arduino Board Ethernet
  RESISTOR_LED = Resistor [tolerance=±5% resistance=47 package="1206 [SMD]"]
  RESISTOR_SIGNAL = Resistor [tolerance=±1% resistance=240 package="1206 [SMD]"]
  PULLDOWN_RESISTOR = Resistor [tolerance=±5% resistance=10k package="1206 [SMD]"]
  RTC = DS1302 [package="DIP8 [THT]"]
  32_768kHz = CRYSTAL [package=crystal-32khz-smd]
  CR2032_3V = Battery Holders [package=battcon_12mm]
  24VDC_/_4-20mA_Device = Screw terminal - 2 pins [package=THT]
  RESISTOR_SIGNAL_2 = Resistor [tolerance=±1% resistance=10 package="1206 [SMD]"]
  LOGGING_SWITCH = Round Pushbutton
  LOGGING_INDICATOR_GREEN_LED = LEDs [package=led10mm]
  24VDC/5VDC = RioRand LM2596
  500mA_Fuse = FUSE [package=fuse_5mm]

nets:
  GND: Arduino.GND, RESISTOR_LED.Pin_1, RESISTOR_SIGNAL.Pin_1, PULLDOWN_RESISTOR.Pin_1, RTC.0V, CR2032_3V.-, 24VDC/5VDC.Pin_2, 24VDC/5VDC.Pin_4
  N1: Arduino.AREF, Arduino.VIN, 24VDC/5VDC.Pin_3
  N2: Arduino.A0, 24VDC_/_4-20mA_Device.pin2, RESISTOR_SIGNAL_2.Pin_0
  N3: Arduino.D2_PWM, RTC.CE_-_Chip_Enable
  N4: Arduino.D3_PWM, RTC.I/O_-_SPI_Data_In/Out
  N5: Arduino.D4, RTC.SCLK_-_SPI_Clock
  N6: Arduino.D5_PWM, PULLDOWN_RESISTOR.Pin_0, LOGGING_SWITCH.leg0
  N7: Arduino.D6_PWM, LOGGING_INDICATOR_GREEN_LED.A
  N8: Arduino.3V3, LOGGING_SWITCH.leg1
  N9: Arduino.5V, RTC.+V
  N10: RESISTOR_LED.Pin_0, LOGGING_INDICATOR_GREEN_LED.C
  N11: RESISTOR_SIGNAL.Pin_0, RESISTOR_SIGNAL_2.Pin_1
  N12: RTC.X1_-_Crystal, 32_768kHz.1
  N13: RTC.X2_-_Crystal, 32_768kHz.2
  N14: RTC.Vbat_-_Backup_Supply, CR2032_3V.+
  N15: 24VDC_/_4-20mA_Device.pin1, 24VDC/5VDC.Pin_1, 500mA_Fuse.2
  24V: 500mA_Fuse.1
